# Fritzing sketch esquema (saved by Fritzing 0.9.4)

parts:
  A1 = Wemos S2 Mini [part_number="WeMos D1 Mini Lite"]
  Component1 = RS485_XY-017 [part_number=XY-017]
  J1 = Camdenboss CTB0158-4 [part_number=CTB0158-4 package=THT]
  Component2 = RS485_XY-017 [part_number=XY-017]
  Component3 = RS485_XY-017 [part_number=XY-017]
  LM7805_IC1 = Voltage Regulator [package=to-220-alt]
  J2 = RJ11 Jack [package=rj11-6]
  J3 = RJ11 Jack [package=rj11-6]
  R4 = Resistor [tolerance=±5% resistance=2k package=THT]
  R5 = Resistor [tolerance=±5% resistance=2k package=THT]
  R6 = Resistor [tolerance=±5% resistance=2k package=THT]
  R7 = Resistor [tolerance=±5% resistance=2k package=THT]

nets:
  N1: A1.Pin_2, Component2.RXD
  N2: A1.Pin_3, Component2.TXD
  N3: A1.Pin_4, Component3.RXD
  N4: A1.Pin_5, Component3.TXD
  N5: A1.Pin_8, Component1.VCC
  N6: A1.Pin_17, LM7805_IC1.OUT
  GND: A1.Pin_18, A1.Pin_26, Component1.GND, J1.terminal_3, Component2.GND, Component3.GND, LM7805_IC1.IN, J2.1, J3.1
  N7: A1.Pin_19, Component1.RXD
  N8: A1.Pin_27, Component1.TXD
  N9: Component1.A, J1.pin1
  N10: Component1.B, J1.pin2
  N11: J1.terminal_4, LM7805_IC1.GND, R4.Pin_0
  N12: Component2.A, J3.5
  N13: Component2.B, J3.6
  N14: Component3.A, J2.5
  N15: Component3.B, J2.6
  N16: J2.2, R5.Pin_1
  N17: J2.3, R7.Pin_1
  N18: J3.2, R6.Pin_1
  N19: J3.3, R4.Pin_1

notes:
  To controller
  Mouser ref 490-P78E05-1000
  12V
  5V
  3V3

custom parts:
  Wemos S2 Mini: A mini wifi board based on the ESP32-S2FN4R2.
  RS485_XY-017: Commercially available RS485 to RS232 TTL Module
